# Fritzing sketch wiring (saved by Fritzing 0.9.9b)
stripboards: 2

parts:
  MCU1 = Raspberry Pi Zero
  Power_plug1 = Power plug
  NEOPIXEL1 = Neopixel Strip -- White (30/m) [part_number=1376]

nets:
  VCC: MCU1.pin_2, MCU1.pin_4, Power_plug1.VCC, NEOPIXEL1.+5V
  N1: MCU1.pin_32, NEOPIXEL1.Din
  GND: Power_plug1.GND, NEOPIXEL1.GND

custom parts:
  Neopixel Strip -- White (30/m): These NeoPixel strips have 30 digitally-addressable pixel LEDs per meter and are very affordable and are only 12.5 mm wide, 10 mm if you remove the strip from the casing.
